# Fritzing sketch SidewinderToUsb (saved by Fritzing 0.9.4)
circuit board: 6.27805cm x 4.4271cm
breadboards: 1

parts:
  C1_001uF = Capacitor [package=cap-pth-large]
  C2_001uF = Capacitor [package=cap-pth-large]
  Teensy_2_0 = Teensy 2.0
  R3_220 = Resistor [tolerance=±5% resistance=220 package=THT]
  R2_2_2k = Resistor [tolerance=±5% resistance=220 package=THT]
  R1_2_2k = Resistor [tolerance=±5% resistance=220 package=THT]
  Gameport = DB15 Connector [package=db15]

nets:
  N1: C1_001uF.1, Teensy_2_0.B4, R2_2_2k.Pin_0
  N2: C1_001uF.2, C2_001uF.2, Teensy_2_0.GND, Gameport.4
  N3: C2_001uF.1, Teensy_2_0.B5, R1_2_2k.Pin_1
  N4: Teensy_2_0.B0, Teensy_2_0.D0, Gameport.2
  N5: Teensy_2_0.B1, Gameport.7
  N6: Teensy_2_0.B2, Gameport.10
  N7: Teensy_2_0.B3, Gameport.14
  N8: Teensy_2_0.D3, R3_220.Pin_0
  N9: Teensy_2_0.VCC, Gameport.1
  N10: R3_220.Pin_1, Gameport.12
  N11: R2_2_2k.Pin_1, Gameport.11, Gameport.13
  N12: R1_2_2k.Pin_0, Gameport.3

custom parts:
  DB15 Connector: DB15 Connector Standard DB15 (D-Sub 15) pc midi or gameport connector. Can be used for old PC compatible joystic.
